# Fritzing sketch ConnectionESP_Arduino (saved by Fritzing 0.9.3b)
breadboards: 1

parts:
  Part1 = Arduino Uno (Rev3)
  U1 = ESP8266 WiFi Module [part_number=ESP8266]
  R2 = Resistor [tolerance=±5% resistance=1k package="0402 [SMD]"]  # not connected
  R3 = Resistor [tolerance=±5% resistance=2.2k package="0402 [SMD]"]
  R4 = Resistor [tolerance=±5% resistance=2.2k package="0603 [SMD]"]
  R4_2 = Resistor [tolerance=±5% resistance=10k package="0805 [SMD]"]

nets:
  N1: Part1.D6_PWM, U1.TXD
  3V3: Part1.3V3, U1.VCC, R4.Pin_1, R4_2.Pin_1
  GND: Part1.GND, U1.GND, R3.Pin_0
  N2: U1.RXD, R3.Pin_1
  N3: U1.CH_PD, R4.Pin_0, R4_2.Pin_0

custom parts:
  ESP8266 WiFi Module: Generic WiFi Module based on the ESP8266 with onboard PCB antenna and UART communications
