# Fritzing sketch Full project (saved by Fritzing 0.9.3b)
breadboards: 2

parts:
  Part1 = Arduino Uno (Rev3)
  U1 = ESP8266 WiFi Module [part_number=ESP8266]
  R2 = Resistor [tolerance=±5% resistance=1k package="0402 [SMD]"]  # not connected
  R3 = Resistor [tolerance=±5% resistance=2.2k package="0402 [SMD]"]
  R4 = Resistor [tolerance=±5% resistance=2.2k package="0603 [SMD]"]
  R4_2 = Resistor [tolerance=±5% resistance=10k package="0805 [SMD]"]
  Sensore_PIR_HC-SR502 = HC-SR501 Body Sensor Module
  U2 = TMP36 [package=to-92-kit]
  R5 = PHOTOCELL [package=photocell-kit]
  R6 = Resistor [tolerance=±5% resistance=10k package="0402 [SMD]"]
  LED1 = LED - 5mm [color="Red (633nm)" package="5 mm [THT]"]
  LED2 = LED - 5mm [color="Yellow (595nm)" package="5 mm [THT]"]

nets:
  N1: Part1.A0, R5.P$2, R6.Pin_1
  N2: Part1.A1, U2.VOUT
  N3: Part1.D12/MISO, LED2.anode
  N4: Part1.D13/SCK, LED1.anode
  N5: Part1.D1/TX, Sensore_PIR_HC-SR502.OUT
  N6: Part1.D6_PWM, U1.TXD
  3V3: Part1.3V3, U1.VCC, R4.Pin_1, R4_2.Pin_1
  VCC: Part1.5V, Sensore_PIR_HC-SR502.VCC, U2.VCC, R5.P$1
  GND: Part1.GND, U1.GND, R3.Pin_0, Sensore_PIR_HC-SR502.GND, U2.GND, R6.Pin_0, LED1.cathode, LED2.cathode
  N7: U1.RXD, R3.Pin_1
  N8: U1.CH_PD, R4.Pin_0, R4_2.Pin_0

custom parts:
  ESP8266 WiFi Module: Generic WiFi Module based on the ESP8266 with onboard PCB antenna and UART communications
  HC-SR501 Body Sensor Module: Pyroelectric Infrared PIR Motion Sensor Detector Module
