# Fritzing sketch HC-SR501-Arduino (saved by Fritzing 0.9.3b)
breadboards: 1

parts:
  Arduino_UNO = Arduino Uno (Rev3)
  Sensore_PIR_HC-SR501 = HC-SR501 Body Sensor Module
  LED = LED - 5mm [color="Red (633nm)" package="5 mm [THT]"]
  J1 = Piezo Speaker

nets:
  N1: Arduino_UNO.D13/SCK, LED.anode
  GND: Arduino_UNO.GND, Sensore_PIR_HC-SR501.GND, LED.cathode, J1.pin1
  N2: Arduino_UNO.D2, Sensore_PIR_HC-SR501.OUT
  N3: Arduino_UNO.D4, J1.pin2
  5V: Arduino_UNO.5V, Sensore_PIR_HC-SR501.VCC

custom parts:
  HC-SR501 Body Sensor Module: Pyroelectric Infrared PIR Motion Sensor Detector Module
